# Fritzing sketch Schematics (saved by Fritzing 0.9.2b)
breadboards: 2

parts:
  IC1 = Voltage Regulator [package=to220-igo]
  VCC1 = Battery block 9V
  Part2 = SRF05 Ultrasonic Rangefinder
  Part3 = SRF05 Ultrasonic Rangefinder
  Part4 = SRF05 Ultrasonic Rangefinder
  Part5 = SRF05 Ultrasonic Rangefinder
  Part6 = SRF05 Ultrasonic Rangefinder
  R2 = Resistor [tolerance=±5% resistance=220 package=THT]
  Part1 = Arduino Uno (Rev3) - ICSP
  Q1 = npn-Powertransistor [package="TO220 [THT]"]
  Q2 = npn-Powertransistor [package="TO220 [THT]"]
  R3 = Resistor [tolerance=±5% resistance=220 package="0603 [SMD]"]
  M1 = DC Motor
  M2 = DC Motor
  Q3 = PHOTOTRANSISTOR REFLECTIVE OBJECT SENSOR [package=qrb1114-side]
  Q4 = PHOTOTRANSISTOR REFLECTIVE OBJECT SENSOR [package=qrb1114-side]
  R4 = Resistor [tolerance=±5% resistance=220 package="2010 [SMD]"]
  R5 = Resistor [tolerance=±5% resistance=220 package="2010 [SMD]"]
  R6 = Resistor [tolerance=±5% resistance=220 package="2010 [SMD]"]
  R7 = Resistor [tolerance=±5% resistance=220 package="2010 [SMD]"]

nets:
  GND: IC1.GND, VCC1.-, Part2.GND, Part3.GND, Part4.GND, Part5.GND, Part6.GND, Part1.GND, Q1.emitter, Q2.emitter, R4.Pin_0, R5.Pin_1, R6.Pin_1, R7.Pin_0
  N1: IC1.IN, VCC1.+, M1.pin_1, M2.pin_2
  VCC: IC1.OUT, Part2.VCC, Part3.VCC, Part4.VCC, Part5.VCC, Part6.VCC, Part1.5V, Q3.A, Q3.E, Q4.A, Q4.E
  N2: Part2.Trig, Part1.D4
  N3: Part2.Echo, Part1.D9_PWM
  N4: Part3.Trig, Part1.D3_PWM
  N5: Part3.Echo, Part1.D8
  N6: Part4.Trig, Part1.ICSP_MISO, Part1.D12/MISO
  N7: Part4.Echo, Part1.D5_PWM
  N8: Part5.Trig, Part1.D13/SCK
  N9: Part5.Echo, Part1.D6_PWM
  N10: Part6.Trig, Part1.D2
  N11: Part6.Echo, Part1.D7
  N12: R2.Pin_0, Part1.D10_PWM/SS
  N13: R2.Pin_1, Q2.base
  N14: Part1.A0, Q3.C, R6.Pin_0
  N15: Part1.A1, Q4.C, R7.Pin_1
  N16: Part1.ICSP_MOSI, Part1.D11_PWM/MOSI, R3.Pin_0
  N17: Q1.base, R3.Pin_1
  N18: Q1.collector, M2.pin_1
  N19: Q2.collector, M1.pin_2
  N20: Q3.K, R4.Pin_1
  N21: Q4.K, R5.Pin_0
